# Fritzing sketch Brouwerij (saved by Fritzing 0.7.12b)
breadboards: 1

parts:
  Raspberry_Pi1 = Raspberry Pi (Model B)  # not connected
  DS1 = DS18B20 1-Wire Temperature Sensor [part_number=DS18B20]
  Pi1 = Adafruit Pi Cobbler
  R3 = Resistor [tolerance=±5% resistance=10k package=THT]
  LED1 = LED - 5mm [color="Red (633nm)" package="5 mm [THT]"]
  R2 = Resistor [tolerance=±5% resistance=10k package=THT]
  IC1 = IC, DIP package, 14 pins [chip_label=IC]
  R1 = Resistor [tolerance=±5% resistance=4.7k package=THT]

nets:
  VDD: DS1.VDD, Pi1.3V3, R1.Pin_0
  N1: DS1.DQ, Pi1.#4
  GND: DS1.GND, Pi1.GND, R2.Pin_1
  +5V: Pi1.5V0, IC1.pin5
  N2: Pi1.#18, R3.Pin_0
  N3: R3.Pin_1, IC1.pin4
  N4: LED1.cathode, R2.Pin_0
  N5: LED1.anode, IC1.pin3

notes:
  DS18B20:
  GND (white)
  DQ (blue/white)
  VDD (orange/white)
  Brewgear-Pi, Homebrew brewery automation, 1

custom parts:
  Raspberry Pi (Model B): Raspberry Pi Single-board Computer, Model B
  Adafruit Pi Cobbler: Adafruit Pi Cobbler GPIO Breakout for Raspberry Pi
